# Fritzing sketch arduino_pi (saved by Fritzing 0.9.3b)
breadboards: 1

parts:
  Raspberry_Pi_1 = Raspberry Pi 3 [part_number=RPI-3-V1.2]
  Part1 = Arduino Uno (Rev3)  # not connected
  LED1 = LED - 5mm [color="Red (633nm)" package="5 mm [THT]"]

nets:
  N1: Raspberry_Pi_1.GPIO17, LED1.anode
  N2: Raspberry_Pi_1.GND, LED1.cathode

// code stored in the sketch: arduino_pi.ino
    String data="Hello From Arduino!";
     
    void setup() {
      // put your setup code here, to run once:
    Serial.begin(9600);
     
    }
     
    void loop() {
      // put your main code here, to run repeatedly:
      Serial.println(data);//data that is being Sent
      delay(200);
    }
