# Fritzing sketch bluetooth_led_control (saved by Fritzing 0.9.3b)
breadboards: 1

parts:
  Part1 = Arduino Uno (Rev3)
  R1 = Resistor [tolerance=±5% resistance=220 package=THT]
  LED1 = LED - 5mm [color="Red (633nm)" package="5 mm [THT]"]
  Part2 = Bluetooth HC-05 Macho

nets:
  N1: Part1.D13/SCK, R1.Pin_1
  GND: Part1.GND, LED1.cathode, Part2.GND
  N2: Part1.D0/RX, Part2.TXD
  N3: Part1.D1/TX, Part2.RXD
  5V: Part1.5V, Part2.VCC
  N4: R1.Pin_0, LED1.anode

// code stored in the sketch: bluetooth_led_control.ino
char junk;
String inputString="";

void setup()                    // run once, when the sketch starts
{
 Serial.begin(9600);            // set the baud rate to 9600, same should be of your Serial Monitor
 pinMode(13, OUTPUT);
}

void loop()
{
  if(Serial.available()){
  while(Serial.available())
    {
      char inChar = (char)Serial.read(); //read the input
      inputString += inChar;        //make a string of the characters coming on serial
    }
    Serial.println(inputString);
    while (Serial.available() > 0)  
    { junk = Serial.read() ; }      // clear the serial buffer
    if(inputString == "a"){         //in case of 'a' turn the LED on
      digitalWrite(13, HIGH);  
    }else if(inputString == "b"){   //incase of 'b' turn the LED off
      digitalWrite(13, LOW);
    }
    inputString = "";
  }
}
