# Fritzing sketch motion_detector (saved by Fritzing 0.9.3b)
breadboards: 1

parts:
  PIR1 = PIR sensor
  Part1 = Arduino Uno (Rev3)
  J1 = Piezo Speaker

nets:
  N1: PIR1.VDD, Part1.D2
  N2: PIR1.SIG, Part1.5V
  GND: PIR1.GND, Part1.GND, J1.pin1
  N3: Part1.D9_PWM, J1.pin2
